# Fritzing sketch wiring (saved by Fritzing 0.9.10b)

parts:
  Part1 = Arduino Uno (Rev3)
  Mod1 = Raspberry Pi 4B  # not connected
  Part2 = Thumb Joystick
  Part3 = InvenSense MPU6050

nets:
  N1: Part1.A0, Part2.VERT
  N2: Part1.A1, Part2.HORZ
  N3: Part1.A4/SDA, Part3.SDA
  N4: Part1.A5/SCL, Part3.SCL
  3V3: Part1.3V3, Part3.VCC
  5V: Part1.5V, Part2.VCC
  GND: Part1.GND, Part2.GND, Part3.GND
